// Logisim project app.circ as structural Verilog: 1 circuit, main circuit main
module main (
);

  wire clock_1_out;
  wire [31:0] main_1_out_2, main_1_out_3, main_1_out_4, main_1_out_5, main_1_out_6, main_1_out_7,
       main_1_out_8, main_1_out_9, main_1_out_10, main_1_out_11, main_1_out_12, main_1_out_13, main_1_out_14,
       main_1_out_15, main_1_out_16, main_1_out_17, main_1_out_18, main_1_out_19, main_1_out_20,
       main_1_out_21, main_1_out_22, main_1_out_23, main_1_out_24, main_1_out_25, main_1_out_26,
       main_1_out_27, main_1_out_28, main_1_out_29, main_1_out_30, main_1_out_31, main_1_out_32,
       main_1_out_33, main_1_out_34, main_1_out_35, main_1_out_36, main_1_out_37, main_1_out_38,
       main_1_out_39, main_1_out_40, main_1_out_41, main_1_out_42, main_1_out_43, main_1_out_44,
       main_1_out_45, main_1_out_46, main_1_out_47, main_1_out_48, main_1_out_49, main_1_out_50,
       main_1_out_51, main_1_out_52, main_1_out_53, main_1_out_54, main_1_out_55, main_1_out_56,
       main_1_out_57, main_1_out_58, main_1_out_59, main_1_out_60, main_1_out_61, main_1_out_62,
       main_1_out_63, main_1_out_64, main_1_out_65, main_1_out_66, main_1_out_67, main_1_out_68,
       main_1_out_69, main_1_out_70, main_1_out_71, main_1_out_72, main_1_out_73, main_1_out_74,
       main_1_out_75, main_1_out_76, main_1_out_77, main_1_out_78, main_1_out_79, main_1_out_80,
       main_1_out_81, main_1_out_82, main_1_out_83, main_1_out_84, main_1_out_85, main_1_out_86,
       main_1_out_87, main_1_out_88, main_1_out_89, main_1_out_90, main_1_out_91, main_1_out_92,
       main_1_out_93, main_1_out_94, main_1_out_95, main_1_out_96, main_1_out_97, main_1_out_98,
       main_1_out_99, main_1_out_100, main_1_out_101, main_1_out_102, main_1_out_103, main_1_out_104,
       main_1_out_105, main_1_out_106, main_1_out_107, main_1_out_108, main_1_out_109, main_1_out_110,
       main_1_out_111, main_1_out_112, main_1_out_113, main_1_out_114, main_1_out_115, main_1_out_116,
       main_1_out_117, main_1_out_118, main_1_out_119, main_1_out_120, main_1_out_121, main_1_out_122,
       main_1_out_123, main_1_out_124, main_1_out_125, main_1_out_126, main_1_out_127, main_1_out_128,
       main_1_out_129;

  DotMatrix #(.matrixcols(32), .matrixrows(32), .persist(512)) dotmatrix_1 (
    .col0(main_1_out_2), .col1(main_1_out_3), .col2(main_1_out_4), .col3(main_1_out_5), .col4(main_1_out_6),
    .col5(main_1_out_7), .col6(main_1_out_8), .col7(main_1_out_9), .col8(main_1_out_10),
    .col9(main_1_out_11), .col10(main_1_out_12), .col11(main_1_out_13), .col12(main_1_out_14),
    .col13(main_1_out_15), .col14(main_1_out_16), .col15(main_1_out_17), .col16(main_1_out_18),
    .col17(main_1_out_19), .col18(main_1_out_20), .col19(main_1_out_21), .col20(main_1_out_22),
    .col21(main_1_out_23), .col22(main_1_out_24), .col23(main_1_out_25), .col24(main_1_out_26),
    .col25(main_1_out_27), .col26(main_1_out_28), .col27(main_1_out_29), .col28(main_1_out_30),
    .col29(main_1_out_31), .col30(main_1_out_32), .col31(main_1_out_33));
  Clock clock_1 (.out(clock_1_out));
  logic_main main_1 (
    .out_2(main_1_out_2), .out_3(main_1_out_3), .out_4(main_1_out_4), .out_5(main_1_out_5),
    .out_6(main_1_out_6), .out_7(main_1_out_7), .out_8(main_1_out_8), .out_9(main_1_out_9),
    .out_10(main_1_out_10), .out_11(main_1_out_11), .out_12(main_1_out_12), .out_13(main_1_out_13),
    .out_14(main_1_out_14), .out_15(main_1_out_15), .out_16(main_1_out_16), .out_17(main_1_out_17),
    .out_18(main_1_out_18), .out_19(main_1_out_19), .out_20(main_1_out_20), .out_21(main_1_out_21),
    .out_22(main_1_out_22), .out_23(main_1_out_23), .out_24(main_1_out_24), .out_25(main_1_out_25),
    .out_26(main_1_out_26), .out_27(main_1_out_27), .out_28(main_1_out_28), .out_29(main_1_out_29),
    .out_30(main_1_out_30), .out_31(main_1_out_31), .out_32(main_1_out_32), .out_33(main_1_out_33),
    .out_34(main_1_out_34), .out_35(main_1_out_35), .out_36(main_1_out_36), .out_37(main_1_out_37),
    .out_38(main_1_out_38), .out_39(main_1_out_39), .out_40(main_1_out_40), .out_41(main_1_out_41),
    .out_42(main_1_out_42), .out_43(main_1_out_43), .out_44(main_1_out_44), .out_45(main_1_out_45),
    .out_46(main_1_out_46), .out_47(main_1_out_47), .out_48(main_1_out_48), .out_49(main_1_out_49),
    .out_50(main_1_out_50), .out_51(main_1_out_51), .out_52(main_1_out_52), .out_53(main_1_out_53),
    .out_54(main_1_out_54), .out_55(main_1_out_55), .out_56(main_1_out_56), .out_57(main_1_out_57),
    .out_58(main_1_out_58), .out_59(main_1_out_59), .out_60(main_1_out_60), .out_61(main_1_out_61),
    .out_62(main_1_out_62), .out_63(main_1_out_63), .out_64(main_1_out_64), .out_65(main_1_out_65),
    .out_66(main_1_out_66), .out_67(main_1_out_67), .out_68(main_1_out_68), .out_69(main_1_out_69),
    .out_70(main_1_out_70), .out_71(main_1_out_71), .out_72(main_1_out_72), .out_73(main_1_out_73),
    .out_74(main_1_out_74), .out_75(main_1_out_75), .out_76(main_1_out_76), .out_77(main_1_out_77),
    .out_78(main_1_out_78), .out_79(main_1_out_79), .out_80(main_1_out_80), .out_81(main_1_out_81),
    .out_82(main_1_out_82), .out_83(main_1_out_83), .out_84(main_1_out_84), .out_85(main_1_out_85),
    .out_86(main_1_out_86), .out_87(main_1_out_87), .out_88(main_1_out_88), .out_89(main_1_out_89),
    .out_90(main_1_out_90), .out_91(main_1_out_91), .out_92(main_1_out_92), .out_93(main_1_out_93),
    .out_94(main_1_out_94), .out_95(main_1_out_95), .out_96(main_1_out_96), .out_97(main_1_out_97),
    .out_98(main_1_out_98), .out_99(main_1_out_99), .out_100(main_1_out_100), .out_101(main_1_out_101),
    .out_102(main_1_out_102), .out_103(main_1_out_103), .out_104(main_1_out_104), .out_105(main_1_out_105),
    .out_106(main_1_out_106), .out_107(main_1_out_107), .out_108(main_1_out_108), .out_109(main_1_out_109),
    .out_110(main_1_out_110), .out_111(main_1_out_111), .out_112(main_1_out_112), .out_113(main_1_out_113),
    .out_114(main_1_out_114), .out_115(main_1_out_115), .out_116(main_1_out_116), .out_117(main_1_out_117),
    .out_118(main_1_out_118), .out_119(main_1_out_119), .out_120(main_1_out_120), .out_121(main_1_out_121),
    .out_122(main_1_out_122), .out_123(main_1_out_123), .out_124(main_1_out_124), .out_125(main_1_out_125),
    .out_126(main_1_out_126), .out_127(main_1_out_127), .out_128(main_1_out_128), .out_129(main_1_out_129),
    .in_1(clock_1_out));
  DotMatrix #(.matrixcols(32), .matrixrows(32), .persist(512)) dotmatrix_2 (
    .col0(main_1_out_66), .col1(main_1_out_67), .col2(main_1_out_68), .col3(main_1_out_69),
    .col4(main_1_out_70), .col5(main_1_out_71), .col6(main_1_out_72), .col7(main_1_out_73),
    .col8(main_1_out_74), .col9(main_1_out_75), .col10(main_1_out_76), .col11(main_1_out_77),
    .col12(main_1_out_78), .col13(main_1_out_79), .col14(main_1_out_80), .col15(main_1_out_81),
    .col16(main_1_out_82), .col17(main_1_out_83), .col18(main_1_out_84), .col19(main_1_out_85),
    .col20(main_1_out_86), .col21(main_1_out_87), .col22(main_1_out_88), .col23(main_1_out_89),
    .col24(main_1_out_90), .col25(main_1_out_91), .col26(main_1_out_92), .col27(main_1_out_93),
    .col28(main_1_out_94), .col29(main_1_out_95), .col30(main_1_out_96), .col31(main_1_out_97));
  DotMatrix #(.matrixcols(32), .matrixrows(32), .persist(512)) dotmatrix_3 (
    .col0(main_1_out_34), .col1(main_1_out_35), .col2(main_1_out_36), .col3(main_1_out_37),
    .col4(main_1_out_38), .col5(main_1_out_39), .col6(main_1_out_40), .col7(main_1_out_41),
    .col8(main_1_out_42), .col9(main_1_out_43), .col10(main_1_out_44), .col11(main_1_out_45),
    .col12(main_1_out_46), .col13(main_1_out_47), .col14(main_1_out_48), .col15(main_1_out_49),
    .col16(main_1_out_50), .col17(main_1_out_51), .col18(main_1_out_52), .col19(main_1_out_53),
    .col20(main_1_out_54), .col21(main_1_out_55), .col22(main_1_out_56), .col23(main_1_out_57),
    .col24(main_1_out_58), .col25(main_1_out_59), .col26(main_1_out_60), .col27(main_1_out_61),
    .col28(main_1_out_62), .col29(main_1_out_63), .col30(main_1_out_64), .col31(main_1_out_65));
  DotMatrix #(.matrixcols(32), .matrixrows(32), .persist(512)) dotmatrix_4 (
    .col0(main_1_out_98), .col1(main_1_out_99), .col2(main_1_out_100), .col3(main_1_out_101),
    .col4(main_1_out_102), .col5(main_1_out_103), .col6(main_1_out_104), .col7(main_1_out_105),
    .col8(main_1_out_106), .col9(main_1_out_107), .col10(main_1_out_108), .col11(main_1_out_109),
    .col12(main_1_out_110), .col13(main_1_out_111), .col14(main_1_out_112), .col15(main_1_out_113),
    .col16(main_1_out_114), .col17(main_1_out_115), .col18(main_1_out_116), .col19(main_1_out_117),
    .col20(main_1_out_118), .col21(main_1_out_119), .col22(main_1_out_120), .col23(main_1_out_121),
    .col24(main_1_out_122), .col25(main_1_out_123), .col26(main_1_out_124), .col27(main_1_out_125),
    .col28(main_1_out_126), .col29(main_1_out_127), .col30(main_1_out_128), .col31(main_1_out_129));
endmodule
