// Logisim project bots.circ as structural Verilog: 1 circuit, main circuit main
module main (
  input  CURR_PLAYER,
  input  PREP_PHASE_END,
  input  CHECKING,
  input  CLR,
  input  WIN,
  input  CLK,
  input  HIT,
  input  [3:0] SHIPS_NUMBER,
  output ROTATED,
  output CONFIRM,
  output [3:0] X,
  output [3:0] Y
);

  wire _1ST_SHOT_DONE, _10SHIPS, and_2_out, BOOT_PHASE, comparator_1_eq, comparator_1_gt,
       controlled_buffer_1_out, counter_1_carry, d_ff_1_q, d_ff_2_qn, demultiplexer_1_out0,
       demultiplexer_1_out1, demultiplexer_1_out2, not_1_out, not_2_out, POSITION_CLOCK, random_1_out,
       ROTATION_CLOCK, SHOOT, SHOOT_PHASE;
  wire [2:0] counter_1_q;
  wire [4:0] counter_2_q;

  Clock clock_1 ();  // open: out
  D_Flip_Flop d_ff_1 (.clk(SHOOT), .D(SHOOT), .Q(d_ff_1_q), .reset(counter_1_carry));  // open: Qn, preset, en
  and and_1 (SHOOT_PHASE, CURR_PLAYER, PREP_PHASE_END);
  not not_1 (not_1_out, PREP_PHASE_END);
  not not_2 (not_2_out, _10SHIPS);
  and and_2 (and_2_out, BOOT_PHASE, CLK);
  Counter #(.width(3), .max('h7)) counter_1 (
    .Q(counter_1_q), .carry(counter_1_carry), .clk(controlled_buffer_1_out), .clr(counter_1_carry));  // open: load, D, count
  assign controlled_buffer_1_out = d_ff_1_q ? CLK : 1'bz;  // Controlled_Buffer controlled_buffer_1
  Pull_Resistor pull_resistor_1 (.node(controlled_buffer_1_out));
  and and_3 (BOOT_PHASE, not_1_out, not_2_out);
  Comparator #(.width(4), .mode("unsigned")) comparator_1 (
    .a(SHIPS_NUMBER), .b(4'b1010), .gt(comparator_1_gt), .eq(comparator_1_eq));  // open: lt
  Demultiplexer #(.select(5)) demultiplexer_1 (
    .out0(demultiplexer_1_out0), .out1(demultiplexer_1_out1), .out2(demultiplexer_1_out2), .in(1'b1),
    .sel(counter_2_q));  // open: out3, out4, out5, out6, out7, out8, out9, out10, out11, out12, out13, out14, out15, out16, out17, out18, out19, out20, out21, out22, out23, out24, out25, out26, out27, out28, out29, out30, out31, en
  Counter #(.width(5), .max('h1f)) counter_2 (
    .Q(counter_2_q), .clk(and_2_out), .clr(CLR));  // open: load, D, count, carry
  Demultiplexer #(.select(3)) demultiplexer_2 (
    .out1(POSITION_CLOCK), .out2(CONFIRM), .in(1'b1), .sel(counter_1_q), .en(d_ff_1_q));  // open: out0, out3, out4, out5, out6, out7
  or or_1 (_10SHIPS, comparator_1_gt, comparator_1_eq);
  assign ROTATION_CLOCK = and_2_out ? demultiplexer_1_out0 : 1'bz;  // Controlled_Buffer controlled_buffer_2
  assign POSITION_CLOCK = and_2_out ? demultiplexer_1_out1 : 1'bz;  // Controlled_Buffer controlled_buffer_3
  assign CONFIRM = and_2_out ? demultiplexer_1_out2 : 1'bz;  // Controlled_Buffer controlled_buffer_4
  D_Flip_Flop d_ff_2 (.clk(SHOOT), .D(SHOOT), .Q(_1ST_SHOT_DONE), .Qn(d_ff_2_qn));  // open: preset, en, reset
  assign SHOOT = d_ff_2_qn ? SHOOT_PHASE : 1'bz;  // Controlled_Buffer controlled_buffer_5
  Counter #(.width(1), .max('h1)) counter_3 (
    .Q(ROTATED), .clk(random_1_out), .clr(CLR));  // open: load, D, count, carry
  Random #(.width(1)) random_1 (.clk(ROTATION_CLOCK), .next(ROTATION_CLOCK), .out(random_1_out));  // open: clr
  random_num_generator_A_main main_1 (.GENERATE(POSITION_CLOCK), .OUTPUT(X));
  random_num_generator_B_main main_2 (.GENERATE(POSITION_CLOCK), .OUTPUT(Y));

  // Other names for the same wires on the sheet: CONFIRM_CLOCK = CONFIRM; SHIP_NUMBER[3:0] = SHIPS_NUMBER
endmodule
