// Logisim project memory_management.circ as structural Verilog: 1 circuit, main circuit main
module main (
  input  [3:0] X,
  input  [3:0] Y,
  input  ROTATED,
  input  [3:0] CHECK_X,
  input  [3:0] CHECK_Y,
  output [14:0] RAM_OUT
);

  wire and_1_out, CHECK, CHECK_OCCUPIED_RST, CHECKING, CLK_2_out, CLK_out, CONFIRM, main_2_p4, main_3_p4,
       main_4_p6, main_4_p7, not_1_out, not_2_out;
  wire [3:0] CURR_SHIP_CHECK, CURRENT_SHIP, MEM_SELECT;
  wire [7:0] demultiplexer_1_out0;
  wire [14:8] SHIP_DATA;

  Button u_CONFIRM (.out(CONFIRM));
  Multiplexer #(.select(2), .width(4), .enable("false")) multiplexer_1 (
    .in0(4'b0001), .in1(4'b0011), .in2(4'b0111), .in3(4'b1111), .out(SHIP_DATA[14:11]), .sel(SHIP_DATA[9:8]));
  assign RAM_OUT = CONFIRM ? {SHIP_DATA[14:11], ROTATED, SHIP_DATA[9:8], Y, X} : 15'bz;  // Controlled_Buffer controlled_buffer_1
  Button u_CHECK (.out(CHECK));
  not not_1 (not_1_out, CONFIRM);
  Clock CLK (.out(CLK_out));
  Demultiplexer #(.width(8), .enable("false")) demultiplexer_1 (
    .out0(demultiplexer_1_out0), .out1(demultiplexer_1_out0), .in(RAM_OUT[7:0]), .sel(RAM_OUT[10]));
  RAM #(.addrWidth(4), .dataWidth(15)) ram_1 (
    .addr(MEM_SELECT), .data(RAM_OUT), .clk(CLK_out), .ld(not_1_out));  // open: sel, clr
  D_Flip_Flop d_ff_1 (.clk(CHECK), .D(CHECK), .Q(CHECKING), .reset(CHECK_OCCUPIED_RST));  // open: Qn, preset, en
  Counter #(.width(4), .max('h9), .trigger("falling")) counter_1 (
    .Q(CURRENT_SHIP), .clk(CONFIRM));  // open: load, D, count, carry, clr
  Counter #(.width(4), .max('h9), .trigger("falling")) counter_2 (
    .Q(CURR_SHIP_CHECK), .carry(CHECK_OCCUPIED_RST), .clk(and_1_out), .clr(CHECK_OCCUPIED_RST));  // open: load, D, count
  and and_1 (and_1_out, CLK_2_out, CHECKING);
  Clock CLK_2 (.out(CLK_2_out));
  assign MEM_SELECT = not_2_out ? CURRENT_SHIP : 4'bz;  // Controlled_Buffer controlled_buffer_2
  not not_2 (not_2_out, CHECKING);
  assign MEM_SELECT = CHECKING ? CURR_SHIP_CHECK : 4'bz;  // Controlled_Buffer controlled_buffer_3
  // _4bit_greater_or_equal_than_and_less_than_main main_1: pin names not known; wires that end beside it: CURRENT_SHIP
  // _4bit_greater_or_equal_than_and_less_than_main main_2: pin names not known; wires that end beside it: 4'b0000, 4'b0100, CURRENT_SHIP, main_2_p4
  // _4bit_greater_or_equal_than_and_less_than_main main_3: pin names not known; wires that end beside it: 4'b0100, 4'b0111, CURRENT_SHIP, main_3_p4
  // _4bit_greater_or_equal_than_and_less_than_main main_4: pin names not known; wires that end beside it: 4'b0111, 4'b1001, CURRENT_SHIP, 4'b1001, 4'b1010, main_4_p6, main_4_p7
  Pull_Resistor pull_resistor_1 (.node(SHIP_DATA[9:8]));
  assign SHIP_DATA[9:8] = main_2_p4 ? 2'b00 : 2'bz;  // Controlled_Buffer controlled_buffer_4
  assign SHIP_DATA[9:8] = main_3_p4 ? 2'b01 : 2'bz;  // Controlled_Buffer controlled_buffer_5
  Pull_Resistor pull_resistor_2 (.node(SHIP_DATA[9:8]));
  Pull_Resistor pull_resistor_3 (.node(SHIP_DATA[9:8]));
  assign SHIP_DATA[9:8] = main_4_p6 ? 2'b10 : 2'bz;  // Controlled_Buffer controlled_buffer_6
  Pull_Resistor pull_resistor_4 (.node(SHIP_DATA[9:8]));
  assign SHIP_DATA[9:8] = main_4_p7 ? 2'b11 : 2'bz;  // Controlled_Buffer controlled_buffer_7

  // Other names for the same wires on the sheet: SHIP_DATA (some bits) = {ROTATED, Y, X}; SHIP_X[3:0] = X;
  //   SHIP_Y[3:0] = Y; SHIP_TYPE[1:0] = SHIP_DATA[9:8]; IS_ROTATED = ROTATED
endmodule
