// Logisim project not_hit_ram_storage.circ as structural Verilog: 1 circuit, main circuit main
module main (
  input  IF_1__save_input,
  input  CLR,
  input  [3:0] X,
  input  [3:0] Y,
  input  CLK,
  output [3:0] X_2,
  output [3:0] Y_2
);

  wire and_1_out, comparator_1_lt, controlled_buffer_1_out, d_ff_1_q, d_ff_1_qn, d_ff_2_q, not_0, not_1_out,
       or_1_out, STORE_iF_EQUAL;
  wire [7:0] ADDRESS, DATA, ram_1_data, STABLE_COUNTER_q;

  Counter #(.width(1), .max('h1), .ongoal("stay")) count_form_0 (
    .carry(not_0), .clk(IF_1__save_input), .clr(CLR));  // open: load, D, count, Q
  assign controlled_buffer_1_out = not_0 ? IF_1__save_input : 1'bz;  // Controlled_Buffer controlled_buffer_1
  Counter #(.max('h90)) STABLE_COUNTER (
    .Q(STABLE_COUNTER_q), .clk(controlled_buffer_1_out), .clr(CLR));  // open: load, D, count, carry
  Register register_1 (.D({Y, X}), .Q(DATA), .clk(IF_1__save_input), .clr(CLR));  // open: en
  D_Flip_Flop d_ff_1 (.clk(CLK), .D(STORE_iF_EQUAL), .Q(d_ff_1_q), .Qn(d_ff_1_qn));  // open: preset, en, reset
  not not_1 (not_1_out, CLK);
  Comparator comparator_1 (.a(STABLE_COUNTER_q), .b(ADDRESS), .eq(STORE_iF_EQUAL), .lt(comparator_1_lt));  // open: gt
  // NOT_Gate not_2 has open pins: in=STORE_iF_EQUAL, out=open
  and and_1 (and_1_out, d_ff_1_q, d_ff_2_q);
  D_Flip_Flop d_ff_2 (.clk(not_1_out), .D(d_ff_1_qn), .Q(d_ff_2_q));  // open: Qn, preset, en, reset
  or or_1 (or_1_out, and_1_out, comparator_1_lt, CLR);
  assign {Y_2, X_2} = not_0 ? ram_1_data : 8'bz;  // Controlled_Buffer controlled_buffer_2
  RAM #(.bus("separate")) ram_1 (
    .addr(ADDRESS), .din(DATA), .data(ram_1_data), .str(STORE_iF_EQUAL), .clk(CLK), .ld(1'b1), .clr(CLR));  // open: sel
  Counter #(.max('h90)) UNSTABLE_COUNTER (.Q(ADDRESS), .clk(CLK), .clr(or_1_out));  // open: load, D, count, carry

  // Notes on the sheet:
  //   connect to get xxxx instead of 0000 when new value
endmodule
